# Fritzing sketch Sketch_LM335 (saved by Fritzing 0.9.3b)
breadboards: 1

parts:
  Componente1 = Arduino Uno (Rev3)
  LED1 = LED - 5mm [color="Red (633nm)" package="5 mm [THT]"]
  LED2 = LED - 5mm [color="Green (555nm)" package="5 mm [THT]"]
  R1 = Resistor [tolerance=±5% resistance=220 package=THT]
  R2 = Resistor [tolerance=±5% resistance=220 package=THT]
  T1 = LM35 Temperature Sensor [package="TO92 [THT]"]

nets:
  N1: Componente1.A0, T1.Vout
  N2: Componente1.D13/SCK, LED1.anode
  N3: Componente1.5V, T1.+Vs
  GND: Componente1.GND, R1.Pin_1, R2.Pin_1, T1.GND
  N4: LED1.cathode, R2.Pin_0
  N5: LED2.cathode, R1.Pin_0
